// Logisim project Boolean Algebra.circ as structural Verilog: 1 circuit, main circuit main
module main (
  input  A,
  input  A_2,
  input  B,
  input  B_2,
  input  A_3,
  input  B_3,
  input  A_4,
  input  B_4,
  input  A_5,
  input  A_6,
  input  B_5,
  input  B_6,
  input  B_7,
  input  A_7,
  input  A_8,
  input  B_8
);

  wire and_1_out, and_2_out, and_3_out, and_4_out, not_1_out, not_2_out, not_3_out, not_4_out, not_5_out,
       not_6_out, or_1_out, or_2_out, or_3_out, or_4_out;

  not not_1 (not_1_out, A_3);
  not not_2 (not_2_out, B_4);
  not not_3 (not_3_out, A_7);
  not not_4 (not_4_out, B_8);
  or or_1 (or_1_out, A_2, B_2);
  not not_5 (not_5_out, or_1_out);
  and and_1 (and_1_out, A_5, B_5);
  and and_2 (and_2_out, not_1_out, not_2_out);
  not not_6 (not_6_out, and_1_out);
  or or_2 (or_2_out, not_3_out, not_4_out);
  LED led_1 (.in(not_5_out));
  LED led_2 (.in(and_2_out));
  LED led_3 (.in(not_6_out));
  LED led_4 (.in(or_2_out));
  or or_3 (or_3_out, A, B);
  or or_4 (or_4_out, B_3, A_4);
  and and_3 (and_3_out, A_6, B_6);
  and and_4 (and_4_out, B_7, A_8);
  LED led_5 (.in(or_3_out));
  LED led_6 (.in(or_4_out));
  LED led_7 (.in(and_3_out));
  LED led_8 (.in(and_4_out));

  // Notes on the sheet:
  //   A'
  //   B'
  //   (A+B)'=A'.B'
  //   (AB)'=A'+B'
  //   (A+B)'
  //   (AB)'
  //   A'+B'
  //   A'.B'
  //   A+B=B+A
  //   A.B=B.A
  //   A+B
  //   B+A
  //   A.B
  //   B.A
endmodule
