// Logisim project Demux 2.circ as structural Verilog: 1 circuit, main circuit main
module main (
  input  S0,
  input  D
);

  wire and_1_out, and_2_out, not_1_out;

  not not_1 (not_1_out, S0);
  and and_1 (and_1_out, not_1_out, D);
  and and_2 (and_2_out, S0, D);
  LED led_1 (.in(and_1_out));
  LED led_2 (.in(and_2_out));
endmodule
