// Logisim project Demux 4.circ as structural Verilog: 1 circuit, main circuit main
module main (
  input  S0,
  input  D,
  input  S1
);

  wire and_1_out, and_2_out, and_3_out, and_4_out, not_1_out, not_2_out;

  not not_1 (not_1_out, S0);
  not not_2 (not_2_out, S1);
  and and_1 (and_1_out, not_1_out, D, not_2_out);
  and and_2 (and_2_out, not_1_out, S1, D);
  and and_3 (and_3_out, S0, not_2_out, D);
  and and_4 (and_4_out, S1, D, S0);
  LED led_1 (.in(and_1_out));
  LED led_2 (.in(and_2_out));
  LED led_3 (.in(and_3_out));
  LED led_4 (.in(and_4_out));

  // Notes on the sheet:
  //   DEMULTIPLEXER 1:4
endmodule
