// Logisim project Demux 8.circ as structural Verilog: 1 circuit, main circuit main
module main (
  input  in_1,
  input  in_2,
  input  in_3,
  input  in_4
);

  wire not_1_out, not_3_out;

  not not_1 (not_1_out, in_2);
  // NOT_Gate not_2 is placed but not wired
  not not_3 (not_3_out, in_4);
endmodule
