// Logisim project Distributive law.circ as structural Verilog: 1 circuit, main circuit main
module main (
  input  A,
  input  A_2,
  input  B,
  input  B_2,
  input  C,
  input  C_2,
  input  A_3,
  input  A_4,
  input  B_3,
  input  B_4,
  input  A_5,
  input  A_6,
  input  C_3,
  input  C_4
);

  wire and_1_out, and_2_out, and_3_out, and_4_out, and_5_out, or_1_out, or_2_out, or_3_out, or_4_out,
       or_5_out;

  and and_1 (and_1_out, B_2, C_2);
  or or_1 (or_1_out, A_3, B_3);
  or or_2 (or_2_out, A_5, C_3);
  or or_3 (or_3_out, A_2, and_1_out);
  LED led_1 (.in(or_3_out));
  and and_2 (and_2_out, or_1_out, or_2_out);
  LED led_2 (.in(and_2_out));
  or or_4 (or_4_out, B, C);
  and and_3 (and_3_out, A_4, B_4);
  and and_4 (and_4_out, A_6, C_4);
  and and_5 (and_5_out, A, or_4_out);
  or or_5 (or_5_out, and_3_out, and_4_out);
  LED led_3 (.in(and_5_out));
  LED led_4 (.in(or_5_out));

  // Notes on the sheet:
  //   BC
  //   A+B
  //   A+C
  //   A+BC=(A+B)(A+C)
  //   A+BC
  //   (A+B).(A+C)
  //   B+C
  //   AB
  //   AC
  //   A(B+C)=AB+AC
  //   A(B+C)
  //   AB+AC
endmodule
