// Logisim project Flip Flop.circ as structural Verilog: 1 circuit, main circuit main
module main (
  input  J,
  input  D,
  input  K,
  input  S,
  input  T,
  input  R,
  output Q,
  output Q_2,
  output out_9,
  output Q_prime,
  output Q_3,
  output Q_4,
  output out_13,
  output out_14
);

  wire clock_1_out, clock_2_out, clock_3_out, clock_4_out;

  Clock clock_1 (.out(clock_1_out));
  Clock clock_2 (.out(clock_2_out));
  J_K_Flip_Flop j_k_ff_1 (.J(J), .clk(clock_1_out), .K(K), .Q(Q_2), .Qn(Q_prime));  // open: preset, en, reset
  S_R_Flip_Flop s_r_ff_1 (.S(S), .clk(clock_2_out), .R(R), .Q(Q_4), .Qn(out_14));  // open: preset, reset, en
  Clock clock_3 (.out(clock_3_out));
  Clock clock_4 (.out(clock_4_out));
  D_Flip_Flop d_ff_1 (.clk(clock_3_out), .D(D), .Q(Q), .Qn(out_9));  // open: preset, en, reset
  T_Flip_Flop t_ff_1 (.clk(clock_4_out), .T(T), .Q(Q_3), .Qn(out_13));  // open: preset, reset, en
endmodule
