// Logisim project Full Subtractor.circ as structural Verilog: 1 circuit, main circuit main
module main (
  input  A,
  input  C,
  input  B
);

  wire and_1_out, and_2_out, and_3_out, not_1_out, or_1_out;

  not not_1 (not_1_out, A);
  and and_1 (and_1_out, not_1_out, C);
  and and_2 (and_2_out, not_1_out, B);
  and and_3 (and_3_out, B, C);
  or or_1 (or_1_out, and_1_out, and_2_out, and_3_out);
  LED led_1 (.in(or_1_out));
endmodule
