// Logisim project Half Adder.circ as structural Verilog: 1 circuit, main circuit main
module main (
  input  in_1,
  input  in_2,
  input  A,
  input  B
);

  wire and_1_out, and_2_out, and_3_out, not_1_out, not_2_out, or_1_out, xor_1_out;

  not not_1 (not_1_out, in_1);
  not not_2 (not_2_out, in_2);
  and and_1 (and_1_out, not_1_out, in_2);
  and and_2 (and_2_out, in_1, not_2_out);
  xor xor_1 (xor_1_out, A, B);
  and and_3 (and_3_out, A, B);
  LED led_1 (.in(xor_1_out));
  LED led_2 (.in(and_3_out));
  or or_1 (or_1_out, and_1_out, and_2_out);
  LED led_3 (.in(or_1_out));

  // Notes on the sheet:
  //   OR
  //   AB'+A'B
  //   AB
endmodule
