// Logisim project Multiplexer 2.circ as structural Verilog: 1 circuit, main circuit main
module main (
  input  D0,
  input  S,
  input  D1
);

  wire and_1_out, and_2_out, not_1_out, or_1_out;

  not not_1 (not_1_out, S);
  and and_1 (and_1_out, D0, not_1_out);
  and and_2 (and_2_out, S, D1);
  or or_1 (or_1_out, and_1_out, and_2_out);
  LED led_1 (.in(or_1_out));
endmodule
