// Logisim project RIPPLE COUNTER.circ as structural Verilog: 1 circuit, main circuit main
module main (
  input  in_1,
  input  in_2,
  output out_3,
  output out_4,
  output out_5,
  output out_6,
  output out_7,
  output out_8
);

  wire clock_1_out;

  Clock clock_1 (.out(clock_1_out));
  T_Flip_Flop t_ff_1 (.clk(clock_1_out), .T(in_1), .Q(out_3));  // open: Qn, preset, reset, en
  J_K_Flip_Flop j_k_ff_1 (.J(in_2), .clk(clock_1_out), .K(in_2), .Q(out_5));  // open: Qn, preset, en, reset
  J_K_Flip_Flop j_k_ff_2 (.J(in_2), .clk(out_5), .K(in_2), .Q(out_6));  // open: Qn, preset, en, reset
  T_Flip_Flop t_ff_2 (.clk(out_3), .T(in_1), .Q(out_4));  // open: Qn, preset, reset, en
  J_K_Flip_Flop j_k_ff_3 (.J(in_2), .clk(out_6), .K(in_2), .Q(out_7));  // open: Qn, preset, en, reset
  J_K_Flip_Flop j_k_ff_4 (.J(in_2), .clk(out_7), .K(in_2), .Q(out_8));  // open: Qn, preset, en, reset
endmodule
