// Logisim project multiplexer 8.circ as structural Verilog: 1 circuit, main circuit main
module main (
  input  S1,
  input  S2,
  input  S0,
  input  D0,
  input  D1,
  input  D2,
  input  D3,
  input  D4,
  input  in_9,
  input  D6,
  input  in_11
);

  wire and_1_out, and_2_out, and_3_out, and_4_out, and_5_out, and_6_out, and_7_out, and_8_out, not_1_out,
       not_2_out, not_3_out, or_1_out;

  not not_1 (not_1_out, S0);
  not not_2 (not_2_out, S1);
  not not_3 (not_3_out, S2);
  and and_1 (and_1_out, not_1_out, not_2_out, not_3_out, D0);
  and and_2 (and_2_out, S0, not_2_out, not_3_out, D1);
  and and_3 (and_3_out, not_1_out, S1, not_3_out, D2);
  and and_4 (and_4_out, S0, S1, not_3_out, D3);
  and and_5 (and_5_out, not_1_out, not_2_out, D4);
  and and_6 (and_6_out, not_2_out, S0, in_9);
  and and_7 (and_7_out, not_1_out, S1, D6);
  and and_8 (and_8_out, S0, S1, S2, in_11);
  or or_1 (or_1_out, and_1_out, and_2_out, and_3_out, and_4_out, and_5_out, and_6_out, and_7_out, and_8_out);
  LED led_1 (.in(or_1_out));

  // Notes on the sheet:
  //   D5
  //   D7
endmodule
